# Fritzing sketch espresso_switch (saved by Fritzing 0.9.4)
circuit board: 8.46667cm x 5.64444cm
breadboards: 1

parts:
  WeMos_D1_Mini1 = WeMos D1 Mini
  U1 = TLP621 [package=THT]
  R2 = Resistor [tolerance=±5% resistance=100 package="0805 [SMD]"]
  U2 = RELAY-SOLIDSTATE [package=relay-s108t02]
  R4 = Resistor [tolerance=±5% resistance=100 package="0805 [SMD]"]
  R5 = Resistor [tolerance=±5% resistance=100 package="0805 [SMD]"]
  S1 = Pushbutton [package="[SMD]"]
  JP2 = Header 2 [package=molex-1x2_lock]
  HLK-PM1 = HLK-PM01
  JP3 = Header 2 [package=molex-1x2_lock]
  LED1 = LED - 3mm [color="Red (633nm)" package="3 mm [THT]"]
  JP1 = Header 2 [package=molex-1x2_lock]
  D1 = Rectifier Diode [part_number=1N4001 package="300 mil [THT]"]

nets (from the breadboard view):
  N1: WeMos_D1_Mini1.5V, HLK-PM1.+Vo
  N2: WeMos_D1_Mini1.D2, S1.Pin_3, S1.Pin_4
  N3: WeMos_D1_Mini1.D4, LED1.cathode
  N4: WeMos_D1_Mini1.D5, U2.+, D1.cathode
  N5: WeMos_D1_Mini1.D6, U1.Pin_3
  N6: WeMos_D1_Mini1.G, U1.Pin_4, R4.Pin_1, R5.Pin_1, S1.Pin_1, S1.Pin_2, HLK-PM1.-Vo, D1.anode
  N7: U1.Pin_1, JP2.1
  N8: U1.Pin_2, R2.Pin_0
  N9: R2.Pin_1, JP2.2
  N10: U2.T1, JP1.1
  N11: U2.T2, JP1.2
  N12: U2.-, R4.Pin_0
  N13: R5.Pin_0, LED1.anode
  N14: HLK-PM1.AC#0, JP3.1
  N15: HLK-PM1.AC#1, JP3.2

notes:
  Power Sense (D6) - power sense with optocoupler. Pullup configuration
  button (D2) - reset settings button, hold 10s to activate and reset wifi & homekit, press to toggle espresso power. Pullup configuration
  Relay (D5) - output for the espresso momentary switch circuit
  LED (D4) - indicates the status of the device
  banded wires are (from left to right): DC power sense (up to 30V), Relay for power toggle and AC Mains supply voltage
