# Fritzing sketch espresso_switch (saved by Fritzing 0.9.3b)
circuit board: 8.46667cm x 5.64444cm
breadboards: 1

parts:
  WeMos_D1_Mini1 = WeMos D1 Mini
  U1 = TLP621 [package=THT]
  R1 = Resistor [tolerance=±5% resistance=100 package="1206 [SMD]"]
  R2 = Resistor [tolerance=±5% resistance=100 package="0805 [SMD]"]
  R3 = Resistor [tolerance=±5% resistance=33k package="1206 [SMD]"]
  U2 = RELAY-SOLIDSTATE [package=relay-s108t02]
  R4 = Resistor [tolerance=±5% resistance=100 package="0805 [SMD]"]
  R5 = Resistor [tolerance=±5% resistance=100 package="0805 [SMD]"]
  J2 = Screw terminal - 2 pins [package=THT]
  S1 = Pushbutton [package="[SMD]"]
  JP1 = Header 2 [package=molex-1x2_lock]
  JP2 = Header 2 [package=molex-1x2_lock]
  HLK-PM1 = HLK-PM01
  JP3 = Header 2 [package=molex-1x2_lock]
  LED1 = LED - 3mm [color="Red (633nm)" package="3 mm [THT]"]

nets (from the breadboard view):
  N1: WeMos_D1_Mini1.3V3, R1.Pin_0
  N2: WeMos_D1_Mini1.D2, S1.Pin_3, S1.Pin_4
  N3: WeMos_D1_Mini1.D4, LED1.cathode
  N4: WeMos_D1_Mini1.D5, U2.+
  N5: WeMos_D1_Mini1.D6, U1.Pin_4, R1.Pin_1
  N6: WeMos_D1_Mini1.G, R3.Pin_0, R4.Pin_1, R5.Pin_1, J2.pin2, S1.Pin_1, S1.Pin_2, JP2.2, HLK-PM1.-Vo
  N7: U1.Pin_1, R2.Pin_1
  N8: U1.Pin_2, J2.pin1, JP2.1
  N9: R2.Pin_0, HLK-PM1.+Vo
  N10: U2.T1, JP1.1
  N11: U2.T2, JP1.2
  N12: U2.-, R4.Pin_0
  N13: R5.Pin_0, LED1.anode
  N14: HLK-PM1.AC#0, JP3.1
  N15: HLK-PM1.AC#1, JP3.2

notes:
  terminal - espresso power sense (default = off)
  button - reset settings button, hold 10s to activate and reset wifi + homekit, press to toggle espresso power
  relay - output for the espresso momentary switch circuit
  LED indicates the status of the device
  banded wires extend from the terminal and the relay for DC power sense and AC/DC power toggle respectively. Green banded wires are for the AC mains power input
